// Digital circuit NAND GATE.dig as structural Verilog
module NAND_GATE (
  input  Input_A,
  input  Input_B
);

  wire N_channel_FET_s, nfet_1_s, P_channel_FET_d, P_channel_FET_s;

  PFET P_channel_FET (.G(Input_A), .S(P_channel_FET_s), .D(P_channel_FET_d));
  PFET pfet_1 (.G(Input_B), .S(P_channel_FET_s), .D(P_channel_FET_d));
  NFET N_channel_FET (.G(Input_A), .D(P_channel_FET_d), .S(N_channel_FET_s));
  NFET nfet_1 (.G(Input_B), .D(N_channel_FET_s), .S(nfet_1_s));

  // Notes on the sheet:
  //   VDD
  //   Output
  //   GND
endmodule
