// Digital circuit ADDER.dig as structural Verilog
module ADDER (
  input  A1,
  input  B1,
  input  C1,
  input  A2,
  input  B2,
  input  A3,
  input  B3,
  input  A4,
  input  B4,
  output S1,
  output S2,
  output S3,
  output S4,
  output C5
);

  wire fa_1_c_out, fa_2_c_out, fa_3_c_out;

  FA fa_1 (.A(A1), .B(B1), .C_in(C1), .S(S1), .C_out(fa_1_c_out));
  FA fa_2 (.A(A2), .B(B2), .C_in(fa_1_c_out), .S(S2), .C_out(fa_2_c_out));
  FA fa_3 (.A(A3), .B(B3), .C_in(fa_2_c_out), .S(S3), .C_out(fa_3_c_out));
  FA fa_4 (.A(A4), .B(B4), .C_in(fa_3_c_out), .S(S4), .C_out(C5));

  // Notes on the sheet:
  //   Ren Fukuoka - 4-bit adder
  //   C2
  //   My custom full adder instances
  //   From Components > Custom
  //   C3
  //   C4
endmodule
