// Digital circuit HA.dig as structural Verilog
module HA (
  input  A,
  input  B,
  output S,
  output C_out
);

  xor xor_1 (S, A, B);
  and and_1 (C_out, A, B);

  // Notes on the sheet:
  //   Ren Fukuoka - Half adder
endmodule
